# Fritzing sketch servo (saved by Fritzing 0.9.10b)

parts:
  Part1 = Arduino Uno (Rev3)
  SERVO2 = Tower Pro SG90 servo [part_number=101246]

nets:
  N1: Part1.D3_PWM, SERVO2.Signal
  5V: Part1.5V, SERVO2.+5V
  GND: Part1.GND, SERVO2.GND

custom parts:
  Tower Pro SG90 servo: Original file by John De Cristofaro http://www.adafruit.com/products/1449 Adafruit Feedback Servo (Small) Edited by: e-radionica.com 28/9/2015
