# Fritzing sketch stepper (saved by Fritzing 0.9.10b)

parts:
  Part1 = Arduino Uno (Rev3)
  Driver2 = 28BYJ-48 Driver Module [part_number=ULN2003 package=THT]
  SM2 = 28BYJ-48 Stepper Motor [part_number=28BYJ-48]

nets:
  N1: Part1.D8, Driver2.IN1
  N2: Part1.D9_PWM, Driver2.IN2
  N3: Part1.D10_PWM/SS, Driver2.IN3
  N4: Part1.D11_PWM/MOSI, Driver2.IN4
  GND: Part1.GND, Driver2.GND
  N5: Part1.VIN, Driver2.Vmotor
  N6: Driver2.blue-pin, SM2.blue-pin
  N7: Driver2.pink-pin, SM2.pink-pin
  N8: Driver2.yellow-pin, SM2.yellow-pin
  N9: Driver2.orange-pin, SM2.orange-pin
  N10: Driver2.red-pin, SM2.red-pin

custom parts:
  28BYJ-48 Driver Module: ULN2003 Driver Module for the 28BYJ-48 Unipolar Stepper Motor LED A - Blue wire - Bottom coil left LED B - Pink wire - Top coil left LED C - Yellow wire - Bottom coil right LED D - Orange wire - Top coil right Common rail - red Connector pins: blue - pink - yellow - orange - red Control pins - IN1 to IN4 Power pins - GND & Vmotor (5-12V) On/Off jumper (if removed, power to motor is cut).
  28BYJ-48 Stepper Motor: Unipolar Stepper Motor 28BYJ-48 Top coil - pink & orange Bottom coil - blue & yellow Common rail - red Connector pins: blue - pink - yellow - orange - red
